# Fritzing sketch 2 wheel (saved by Fritzing 0.9.3b)
breadboards: 1

parts:
  M2 = DC Motor
  VCC1 = Battery
  VCC2 = Battery
  VCC3 = Battery
  VCC4 = Battery
  M4 = DC Motor
  Part3 = Arduino Uno (Rev3)
  S1 = H-Bridge with L298N
  J1 = Infrared Proximity Sensor
  J2 = Infrared Proximity Sensor

nets:
  N1: M2.pin_1, S1.M1-01
  N2: M2.pin_2, S1.M1-02
  N3: VCC1.-, VCC2.+
  N4: VCC1.+, S1.12V
  N5: VCC2.-, VCC3.+
  N6: VCC3.-, VCC4.+
  GND: VCC4.-, Part3.GND, S1.GND, J1.GND, J2.GND
  N7: M4.pin_1, S1.M2-02
  N8: M4.pin_2, S1.M2-01
  N9: Part3.D8, S1.IN2
  N10: Part3.D9_PWM, S1.IN1
  N11: Part3.D10_PWM/SS, S1.ENA
  N12: Part3.D2, J1.Vout
  N13: Part3.D5_PWM, S1.ENB
  N14: Part3.D6_PWM, S1.IN4
  N15: Part3.D7, S1.IN3
  5V: Part3.5V, S1.5V, J1.Vcc, J2.Vcc

custom parts:
  H-Bridge with L298N: h-bridge
